# Fritzing sketch ax-12a-bench-test (saved by Fritzing 1.0.7)
breadboards: 1

parts:
  Adafruit_Feather_ESP32-C1 = Adafruit Feather ESP32-C6 [mn=Adafruit mpn=#5933 part_number=#5933]
  IC1 = 74LVC245 Octal 2-Way Tranceiver
  R2 = Resistor [tolerance=±5% resistance=2.2k package="2010 [SMD]"]
  AX-12A = Header 3 [package=jst-3-smd]
  MEAN_WELL_LRS-50-12_12V_IN = Screw terminal - 2 pins [package=THT]
  R3 = Resistor [tolerance=±5% resistance=1k package="2010 [SMD]"]

nets:
  GND: Adafruit_Feather_ESP32-C1.GND, Adafruit_Feather_ESP32-C1.VBAT, IC1.GND, IC1.!OE, R2.Pin_1, MEAN_WELL_LRS-50-12_12V_IN.pin2
  N1: Adafruit_Feather_ESP32-C1.3.3V, IC1.B2, IC1.B1, AX-12A.1
  N2: Adafruit_Feather_ESP32-C1.IO15, IC1.A1
  N3: Adafruit_Feather_ESP32-C1.IO14, IC1.A2, R2.Pin_0, R3.Pin_0, R3.Pin_1
  N4: Adafruit_Feather_ESP32-C1.IO8, IC1.DIR

notes:
  file: ax-12a-bench-test.fzz
  version: 1
  last updated: 30 June 2026 23:22
  author: Willem van Heemstra
  +12 Volt
  +5 Volt
