# Fritzing sketch psu-verification_v1 (saved by Fritzing 1.0.7)
breadboards: 1

parts:
  Adafruit_Feather_ESP32-C1 = Adafruit Feather ESP32-C6 [mn=Adafruit mpn=#5933 part_number=#5933]  # not connected
  IC1 = 74LVC245 Octal 2-Way Tranceiver  # not connected
  Resistor_(1k) = Resistor [tolerance=±5% resistance=1k package="2010 [SMD]"]
  R2 = Resistor [tolerance=±5% resistance=220 package="2010 [SMD]"]  # not connected
  JP1 = Header 3 [package=jst-3-smd]  # not connected
  LED = LED - 3mm [color="Red (633nm)" current=0.030A package="3 mm [THT]"]
  LRS-50-12_12V_IN = Screw terminal - 2 pins [package=THT]

nets:
  N1: Resistor_(1k).Pin_0, LRS-50-12_12V_IN.pin1
  N2: Resistor_(1k).Pin_1, LED.anode
  N3: LED.cathode, LRS-50-12_12V_IN.pin2

notes:
  Long/Bent Leg "Anode" +
  Short/Straight Leg "Cathode" -
